# Fritzing sketch wiring_diagam (saved by Fritzing 0.9.3b)
breadboards: 1

parts:
  Raspberry_Pi_Zero1 = Raspberry Pi Zero
  S1 = H-Bridge with L298N
  S2 = H-Bridge with L298N
  U1 = LM2596 step down module
  M1 = DC Motor
  M2 = DC Motor
  M3 = DC Motor

nets:
  N1: Raspberry_Pi_Zero1.GPIO17, S2.IN1
  N2: Raspberry_Pi_Zero1.GPIO27, S1.IN3
  N3: Raspberry_Pi_Zero1.GPIO22, S1.IN2
  N4: Raspberry_Pi_Zero1.GND, U1.IN-, U1.OUT-
  N5: Raspberry_Pi_Zero1.GPIO24, S1.IN1
  N6: Raspberry_Pi_Zero1.GPIO23, S1.IN4
  N7: Raspberry_Pi_Zero1.GPIO18, S2.IN2
  N8: Raspberry_Pi_Zero1.5V, U1.OUT+
  N9: S1.M1-01, M1.pin_2
  N10: S1.M1-02, M1.pin_1
  N11: S1.M2-01, M2.pin_2
  N12: S1.M2-02, M2.pin_1
  N13: S2.M2-01, M3.pin_2
  N14: S2.M2-02, M3.pin_1

notes:
  12V Battery
  USB Hub and Camera

custom parts:
  H-Bridge with L298N: h-bridge
  LM2596 step down module: LM2596 DC-DC step down power supply module 3 A.
